// Logisim project A + B = Implementation using 2-4 Decoders.circ as structural Verilog: 1 circuit, main circuit main
module main (
  input  in_1,
  input  in_2,
  output out_3
);

  wire decoder_1_out2, decoder_1_out3;
  wire [1:0] decoder_1_out0, decoder_2_out1;

  Decoder #(.select(2), .enable("false")) decoder_1 (
    .out0(decoder_1_out0[0]), .out1(decoder_1_out0[1]), .out2(decoder_1_out2), .out3(decoder_1_out3),
    .sel({in_2, in_1}));
  Decoder #(.select(2), .enable("false")) decoder_2 (
    .out1(decoder_2_out1[0]), .out3(decoder_2_out1[1]), .sel(decoder_1_out0));  // open: out0, out2
  Decoder #(.select(2), .enable("false")) decoder_3 (.out0(out_3), .sel(decoder_2_out1));  // open: out1, out2, out3
endmodule
