// Logisim project Декодери 2-4 и ИЛИ-порта.circ as structural Verilog: 1 circuit, main circuit main
module main (
  input  A,
  input  B,
  input  C,
  input  D,
  input  E,
  output Y
);

  wire decoder_1_out1, decoder_2_out1, decoder_3_out1, decoder_4_out2;

  Decoder #(.select(2), .enable("false")) decoder_1 (.out1(decoder_1_out1), .sel({D, A}));  // open: out0, out2, out3
  Decoder #(.select(2), .enable("false")) decoder_2 (.out1(decoder_2_out1), .sel({B, A}));  // open: out0, out2, out3
  Decoder #(.select(2), .enable("false")) decoder_3 (.out1(decoder_3_out1), .sel({C, A}));  // open: out0, out2, out3
  Decoder #(.select(2), .enable("false")) decoder_4 (.out2(decoder_4_out2), .sel({E, D}));  // open: out0, out1, out3
  or or_1 (Y, decoder_1_out1, decoder_2_out1, decoder_3_out1, decoder_4_out2);

  // Notes on the sheet:
  //   AD'
  //   AB'
  //   AC'
  //   D'E
endmodule
