// Logisim project Мултиплексери 4-во-1.circ as structural Verilog: 1 circuit, main circuit main
module main (
  input  E,
  input  [1:0] BC,
  input  [1:0] AD,
  input  [1:0] CD
);

  wire multiplexer_3_out, multiplexer_4_out;
  wire [1:0] multiplexer_1_out;

  Multiplexer #(.select(2), .enable("false")) multiplexer_1 (
    .in0(1'b1), .in1(1'b1), .in2(1'b0), .in3(1'b0), .out(multiplexer_1_out[0]), .sel(BC));
  Multiplexer #(.select(2), .enable("false")) multiplexer_2 (
    .in0(1'b1), .in1(1'b1), .in2(1'b0), .in3(1'b0), .out(multiplexer_1_out[1]), .sel(CD));
  Multiplexer #(.select(2), .enable("false")) multiplexer_3 (
    .in0(1'b0), .in1(1'b1), .in2(1'b1), .in3(1'b1), .out(multiplexer_3_out), .sel(multiplexer_1_out));
  Multiplexer #(.select(2), .enable("false")) multiplexer_4 (
    .in0(E), .in1(1'b0), .in2(1'b1), .in3(multiplexer_3_out), .out(multiplexer_4_out), .sel(AD));
  LED Y (.in(multiplexer_4_out));

  // Notes on the sheet:
  //   B'
  //   C'
  //   B'+C'
endmodule
