// Logisim project НИ порти.circ as structural Verilog: 1 circuit, main circuit main
module main (
  input  A,
  input  B,
  input  C,
  input  D,
  input  E,
  output out_6
);

  wire nand_2_out, nand_3_out, nand_4_out, nand_6_out, nand_7_out, nand_8_out, nand_9_out;

  // NAND_Gate nand_1 has open pins: in2=A, in3=A, out=open
  nand nand_2 (nand_2_out, B, B);
  nand nand_3 (nand_3_out, C, C);
  nand nand_4 (nand_4_out, D, D);
  // NAND_Gate nand_5 has open pins: in2=E, in3=E, out=open
  nand nand_6 (nand_6_out, A, nand_2_out);
  nand nand_7 (nand_7_out, A, nand_3_out);
  nand nand_8 (nand_8_out, A, nand_4_out);
  nand nand_9 (nand_9_out, nand_4_out, E);
  nand nand_10 (out_6, nand_6_out, nand_7_out, nand_8_out, nand_9_out);
endmodule
