// Logisim project НИЛИ порти.circ as structural Verilog: 1 circuit, main circuit main
module main (
  input  A,
  input  B,
  input  C,
  input  D,
  input  E,
  output out_6
);

  wire nor_2_out, nor_3_out, nor_4_out, nor_6_out, nor_7_out, nor_8_out;

  // NOR_Gate nor_1 has open pins: in2=A, in3=A, out=open
  nor nor_2 (nor_2_out, B, B);
  nor nor_3 (nor_3_out, C, C);
  nor nor_4 (nor_4_out, D, D);
  // NOR_Gate nor_5 has open pins: in2=E, in3=E, out=open
  nor nor_6 (nor_6_out, nor_2_out, nor_3_out, nor_4_out);
  nor nor_7 (nor_7_out, A, nor_4_out);
  nor nor_8 (nor_8_out, A, E);
  nor nor_9 (out_6, nor_6_out, nor_7_out, nor_8_out);
endmodule
