// Logisim project САМО Декодери 2-4.circ as structural Verilog: 1 circuit, main circuit main
module main (
  input  A,
  input  B,
  input  C,
  input  D,
  input  E,
  output out_6
);

  wire [0:0] decoder_5_out0, decoder_6_out0, decoder_9_out0;
  wire [1:0] decoder_1_out1, decoder_3_out1, decoder_7_out2;

  Decoder #(.select(2), .enable("false")) decoder_1 (.out1(decoder_1_out1[0]), .sel({D, A}));  // open: out0, out2, out3
  Decoder #(.select(2), .enable("false")) decoder_2 (.out1(decoder_1_out1[1]), .sel({B, A}));  // open: out0, out2, out3
  Decoder #(.select(2), .enable("false")) decoder_3 (.out1(decoder_3_out1[0]), .sel({C, A}));  // open: out0, out2, out3
  Decoder #(.select(2), .enable("false")) decoder_4 (.out2(decoder_3_out1[1]), .sel({E, D}));  // open: out0, out1, out3
  Decoder #(.select(2)) decoder_5 (
    .out0(decoder_5_out0[0]), .sel(decoder_1_out1), .en(1'b1));  // open: out1, out2, out3
  Decoder #(.select(2)) decoder_6 (
    .out0(decoder_6_out0[0]), .sel(decoder_3_out1), .en(1'b1));  // open: out1, out2, out3
  Decoder #(.select(2), .enable("false")) decoder_7 (
    .out2(decoder_7_out2[0]), .sel({1'b1, decoder_5_out0[0]}));  // open: out0, out1, out3
  Decoder #(.select(2), .enable("false")) decoder_8 (
    .out2(decoder_7_out2[1]), .sel({1'b1, decoder_6_out0[0]}));  // open: out0, out1, out3
  Decoder #(.select(2)) decoder_9 (
    .out0(decoder_9_out0[0]), .sel(decoder_7_out2), .en(1'b1));  // open: out1, out2, out3
  Decoder #(.select(2), .enable("false")) decoder_10 (
    .out2(out_6), .sel({1'b1, decoder_9_out0[0]}));  // open: out0, out1, out3
endmodule
